# Fritzing sketch Connection (saved by Fritzing 1.0.7)

parts:
  Adafruit_INA228_I2C_Power_Monitor1 = Adafruit INA228 I2C Power Monitor [mn=Adafruit mpn=#5832 part_number=#5832]
  Part1 = XBee Pro RF module
  lps-1 = lps-1

nets:
  N1: Adafruit_INA228_I2C_Power_Monitor1.SCL, lps-1./SCL
  N2: Adafruit_INA228_I2C_Power_Monitor1.GND, lps-1.GND#1
  N3: Adafruit_INA228_I2C_Power_Monitor1.SDA, lps-1./SDA
  N4: Adafruit_INA228_I2C_Power_Monitor1.VCC, lps-1.+3.3V#0
  N5: Part1.VCC, lps-1.+3.3V#12
  N6: Part1.DOUT, lps-1./RxD0
  N7: Part1.DIN, lps-1./TxD0
  N8: Part1.RESET, lps-1./MODEM_RESET
  N9: Part1.GND, lps-1.GND#13
  N10: Part1.ON/SLEEP, lps-1./MODEM_SLEEP

custom parts:
  lps-1: Auto-generated starter part from KiCad board connector model.
